# Fritzing sketch layout (saved by Fritzing 0.9.10b)

parts:
  U1 = lolin
  S1 = Round Pushbutton
  S2 = Toggle Switch [package=THT]
  U2 = Battery Holders [package=lipo-1100mAh]

nets:
  N1: U1.connector11, S1.leg1
  N2: U1.connector15, S1.leg0
  N3: U1.connector16, S2.COM
  N4: U1.connector17, U2.-
  N5: S2.L1, U2.+
